# Fritzing sketch Schema (saved by Fritzing 0.8.7b)

parts:
  Onderdeel1 = Arduino Nano (Rev3.0)
  NEOPIXEL1 = Neopixel Strip -- Black (30/m) [part_number=1376]
  IR1 = TSOP312.., 314.. [package=THT]
  JACK1 = 2.1mm DC Barrel Jack
  S1 = Toggle Switch [package=THT]

nets:
  GND: Onderdeel1.GND, NEOPIXEL1.GND, IR1.GND, JACK1.sleeve
  N1: Onderdeel1.D3, NEOPIXEL1.Din
  N2: Onderdeel1.D11/MOSI, IR1.Data
  VIN: Onderdeel1.VIN, NEOPIXEL1.+5V, S1.L1
  N3: Onderdeel1.5V, IR1.Vs
  N4: JACK1.center, S1.COM

custom parts:
  Neopixel Strip -- Black (30/m): These NeoPixel strips have 30 digitally-addressable pixel LEDs per meter and are very affordable and are only 12.5 mm wide, 10 mm if you remove the strip from the casing.
  2.1mm DC Barrel Jack: 2.1mm DC Barrel Jack with Thru-Hole Connectors (breadboardable)
